// Logisim project washing_pipeline.circ as structural Verilog: 32 circuits, main circuit main
module main (
  input  START,
  input  DOOR_CLOSED,
  input  [1:0] MODE,
  input  [7:0] WATER_LEVEL,
  input  [7:0] TEMP,
  input  [7:0] DRUM_RPM,
  input  CLK,
  input  RESET,
  output VALVE_IN,
  output HEATER,
  output MOTOR_EN_REQ,
  output MOTOR_DIR,
  output PUMP_OUT,
  output DOOR_LOCK,
  output BUZZER,
  output MOTOR_EN_ACTUAL,
  output [7:0] DISPLAY,
  output TRIP,
  output START_PEND,
  output [7:0] TIMER_COUNT,
  output TIMER_MATCH,
  output TIMER_EN,
  output [7:0] PC,
  output [15:0] INSTR,
  output IFID_V,
  output IDEX_V,
  output [7:0] IDEX_PC,
  output EXMEM_V,
  output [7:0] EXMEM_PC,
  output [7:0] ST_ADDR,
  output [7:0] ST_DATA,
  output MEMWB_V,
  output [7:0] MEMWB_PC,
  output [7:0] IFID_PC,
  output WB_WE,
  output [7:0] WB_DATA,
  output [2:0] WB_RD,
  output HALTED,
  output ST_WE,
  output STALL,
  output LOADFWD,
  output FLUSH,
  output [1:0] SEL_A,
  output [1:0] SEL_B
);

  wire ex_stage_1_isbranchtaken, exmem_reg_1_exmem_isld, exmem_reg_1_exmem_isrw, exmem_reg_1_exmem_isst,
       hazard_1_halt_now, hazard_1_idex_vin, hazard_1_ifid_en, hazard_1_ifid_vin, hazard_1_pc_en,
       hazard_1_redirect, id_stage_1_isbeqz, id_stage_1_isbnez, id_stage_1_ishalt, id_stage_1_isimm,
       id_stage_1_isld, id_stage_1_isrw, id_stage_1_isst, id_stage_1_usea, id_stage_1_useb,
       idex_reg_1_idex_isbeqz, idex_reg_1_idex_isbnez, idex_reg_1_idex_ishalt, idex_reg_1_idex_isimm,
       idex_reg_1_idex_isld, idex_reg_1_idex_isrw, idex_reg_1_idex_isst, idex_reg_1_idex_use_a,
       idex_reg_1_idex_use_b, mem_stage_1_p_we_1, memwb_reg_1_memwb_isrw;
  wire [2:0] exmem_reg_1_exmem_rd, id_stage_1_rb, id_stage_1_rd, idex_reg_1_idex_rb, idex_reg_1_idex_rd;
  wire [3:0] mem_stage_1_p_addr_4;
  wire [4:0] id_stage_1_alusignals, idex_reg_1_idex_alusignals;
  wire [7:0] ex_stage_1_aluresult, ex_stage_1_sd, id_stage_1_a, id_stage_1_b, id_stage_1_imm,
       idex_reg_1_idex_a, idex_reg_1_idex_b, idex_reg_1_idex_imm, mem_stage_1_p_wdata_8, mem_stage_1_rdata_8,
       mux2_8_1_y_8, next_pc_1_pc_next_8, peripheral_1_p_rdata_8;
  wire [15:0] ifid_reg_1_ifid_instr;

  NEXT_PC next_pc_1 (
    .isBranchTaken(hazard_1_redirect), .TARGET(idex_reg_1_idex_imm), .PC_8(PC),
    .PC_NEXT_8(next_pc_1_pc_next_8));
  Register PC_REG (.D(next_pc_1_pc_next_8), .en(hazard_1_pc_en), .clk(CLK), .Q(PC), .clr(RESET));
  Register #(.width(1)) register_1 (.D(1'b1), .en(hazard_1_halt_now), .clk(CLK), .Q(HALTED), .clr(RESET));
  ROM #(.dataWidth(16)) rom_1 (.addr(PC), .data(INSTR));
  IFID_REG ifid_reg_1 (
    .V_IN(hazard_1_ifid_vin), .INSTR(INSTR), .PC(PC), .EN(hazard_1_ifid_en), .CLK(CLK), .RESET(RESET),
    .IFID_V(IFID_V), .IFID_INSTR(ifid_reg_1_ifid_instr), .IFID_PC(IFID_PC));
  ID_STAGE id_stage_1 (
    .INSTR_16(ifid_reg_1_ifid_instr), .WB_RD(WB_RD), .WB_DATA(WB_DATA), .WB_WE(WB_WE), .BYP_EN(1'b1),
    .CLK(CLK), .isBNEZ(id_stage_1_isbnez), .isBEQZ(id_stage_1_isbeqz), .aluSignals(id_stage_1_alusignals),
    .isHALT(id_stage_1_ishalt), .isLD(id_stage_1_isld), .isST(id_stage_1_isst), .isRW(id_stage_1_isrw),
    .isImm(id_stage_1_isimm), .useA(id_stage_1_usea), .useB(id_stage_1_useb), .RD(id_stage_1_rd),
    .RB(id_stage_1_rb), .A(id_stage_1_a), .B(id_stage_1_b), .IMM(id_stage_1_imm));
  HAZARD hazard_1 (
    .IFID_V(IFID_V), .IDEX_isLD(idex_reg_1_idex_isld), .RA(id_stage_1_rd), .IDEX_RD(idex_reg_1_idex_rd),
    .USE_A(id_stage_1_usea), .USE_B(id_stage_1_useb), .RB(id_stage_1_rb), .IDEX_V(IDEX_V),
    .TAKEN(ex_stage_1_isbranchtaken), .IDEX_isHALT(idex_reg_1_idex_ishalt), .HALTED(HALTED), .STALL(STALL),
    .IFID_EN(hazard_1_ifid_en), .IDEX_VIN(hazard_1_idex_vin), .REDIRECT(hazard_1_redirect), .FLUSH(FLUSH),
    .HALT_NOW(hazard_1_halt_now), .PC_EN(hazard_1_pc_en), .IFID_VIN(hazard_1_ifid_vin));
  IDEX_REG idex_reg_1 (
    .V_IN(hazard_1_idex_vin), .PC(IFID_PC), .isRW(id_stage_1_isrw), .isImm(id_stage_1_isimm),
    .isLD(id_stage_1_isld), .isST(id_stage_1_isst), .isBEQZ(id_stage_1_isbeqz), .isBNEZ(id_stage_1_isbnez),
    .isHALT(id_stage_1_ishalt), .USE_A(id_stage_1_usea), .USE_B(id_stage_1_useb),
    .aluSignals(id_stage_1_alusignals), .RD(id_stage_1_rd), .RB(id_stage_1_rb), .A(id_stage_1_a),
    .B(id_stage_1_b), .IMM(id_stage_1_imm), .CLK(CLK), .RESET(RESET), .IDEX_V(IDEX_V), .IDEX_PC(IDEX_PC),
    .IDEX_isRW(idex_reg_1_idex_isrw), .IDEX_isImm(idex_reg_1_idex_isimm), .IDEX_isLD(idex_reg_1_idex_isld),
    .IDEX_isST(idex_reg_1_idex_isst), .IDEX_isBEQZ(idex_reg_1_idex_isbeqz),
    .IDEX_isBNEZ(idex_reg_1_idex_isbnez), .IDEX_isHALT(idex_reg_1_idex_ishalt),
    .IDEX_USE_A(idex_reg_1_idex_use_a), .IDEX_USE_B(idex_reg_1_idex_use_b),
    .IDEX_aluSignals(idex_reg_1_idex_alusignals), .IDEX_RD(idex_reg_1_idex_rd), .IDEX_RB(idex_reg_1_idex_rb),
    .IDEX_A(idex_reg_1_idex_a), .IDEX_B(idex_reg_1_idex_b), .IDEX_IMM(idex_reg_1_idex_imm));
  EX_STAGE ex_stage_1 (
    .isBNEZ(idex_reg_1_idex_isbnez), .isBEQZ(idex_reg_1_idex_isbeqz), .A(idex_reg_1_idex_a),
    .B(idex_reg_1_idex_b), .IMM(idex_reg_1_idex_imm), .isImm(idex_reg_1_idex_isimm),
    .aluSignals(idex_reg_1_idex_alusignals), .FWD_W(WB_DATA), .FWD_M(ST_ADDR), .SEL_A(SEL_A), .SEL_B(SEL_B),
    .isBranchTaken(ex_stage_1_isbranchtaken), .aluResult(ex_stage_1_aluresult), .SD(ex_stage_1_sd));
  FORWARD forward_1 (
    .IDEX_USE_A(idex_reg_1_idex_use_a), .IDEX_V(IDEX_V), .EXMEM_isLD(exmem_reg_1_exmem_isld),
    .IDEX_USE_B(idex_reg_1_idex_use_b), .EXMEM_RD(exmem_reg_1_exmem_rd), .IDEX_RD(idex_reg_1_idex_rd),
    .EXMEM_V(EXMEM_V), .EXMEM_isRW(exmem_reg_1_exmem_isrw), .MEMWB_RD(WB_RD), .MEMWB_V(MEMWB_V),
    .MEMWB_isRW(memwb_reg_1_memwb_isrw), .IDEX_RB(idex_reg_1_idex_rb), .LOADFWD(LOADFWD), .SEL_A(SEL_A),
    .SEL_B(SEL_B));
  PERIPHERAL peripheral_1 (
    .TEMP_8(TEMP), .START_1(START), .DOOR_CLOSED_1(DOOR_CLOSED), .MODE_2(MODE), .WATER_LEVEL_8(WATER_LEVEL),
    .DRUM_RPM_8(DRUM_RPM), .P_WDATA_8(mem_stage_1_p_wdata_8), .P_WE_1(mem_stage_1_p_we_1),
    .P_ADDR_4(mem_stage_1_p_addr_4), .CLK(CLK), .RESET_1(RESET), .MOTOR_EN_REQ_1(MOTOR_EN_REQ),
    .PUMP_OUT_1(PUMP_OUT), .VALVE_IN_1(VALVE_IN), .MOTOR_EN_ACTUAL_1(MOTOR_EN_ACTUAL),
    .MOTOR_DIR_1(MOTOR_DIR), .DOOR_LOCK_1(DOOR_LOCK), .HEATER_1(HEATER), .BUZZER_1(BUZZER), .D_TRIP_1(TRIP),
    .DISPLAY_8(DISPLAY), .D_PEND_1(START_PEND), .D_TIMER_EN_1(TIMER_EN), .D_TIMER_MATCH_1(TIMER_MATCH),
    .D_TIMER_COUNT_8(TIMER_COUNT), .P_RDATA_8(peripheral_1_p_rdata_8));
  EXMEM_REG exmem_reg_1 (
    .V_IN(IDEX_V), .PC(IDEX_PC), .isRW(idex_reg_1_idex_isrw), .isLD(idex_reg_1_idex_isld),
    .isST(idex_reg_1_idex_isst), .RD(idex_reg_1_idex_rd), .ALU(ex_stage_1_aluresult), .SD(ex_stage_1_sd),
    .CLK(CLK), .RESET(RESET), .EXMEM_V(EXMEM_V), .EXMEM_PC(EXMEM_PC), .EXMEM_isRW(exmem_reg_1_exmem_isrw),
    .EXMEM_isLD(exmem_reg_1_exmem_isld), .EXMEM_isST(exmem_reg_1_exmem_isst),
    .EXMEM_RD(exmem_reg_1_exmem_rd), .EXMEM_ALU(ST_ADDR), .EXMEM_SD(ST_DATA));
  and and_1 (ST_WE, EXMEM_V, exmem_reg_1_exmem_isst);
  MEM_STAGE mem_stage_1 (
    .ADDR_8(ST_ADDR), .isLD(exmem_reg_1_exmem_isld), .isST(ST_WE), .WDATA_8(ST_DATA),
    .P_RDATA_8(peripheral_1_p_rdata_8), .CLK(CLK), .RDATA_8(mem_stage_1_rdata_8),
    .P_ADDR_4(mem_stage_1_p_addr_4), .P_WE_1(mem_stage_1_p_we_1), .P_WDATA_8(mem_stage_1_p_wdata_8));
  MUX2_8 mux2_8_1 (.B_8(mem_stage_1_rdata_8), .A_8(ST_ADDR), .S_1(exmem_reg_1_exmem_isld), .Y_8(mux2_8_1_y_8));
  MEMWB_REG memwb_reg_1 (
    .V_IN(EXMEM_V), .PC(EXMEM_PC), .isRW(exmem_reg_1_exmem_isrw), .RD(exmem_reg_1_exmem_rd),
    .DATA(mux2_8_1_y_8), .CLK(CLK), .RESET(RESET), .MEMWB_V(MEMWB_V), .MEMWB_PC(MEMWB_PC),
    .MEMWB_isRW(memwb_reg_1_memwb_isrw), .MEMWB_RD(WB_RD), .MEMWB_DATA(WB_DATA));
  and and_2 (WB_WE, MEMWB_V, memwb_reg_1_memwb_isrw);

  // Notes on the sheet:
  //   contents of rom_1 (hex, n*v repeats v):
  //   9800 9ff4 3007 9ffa 3007 9ff5 9901 3107 9ff0 b307 a103 9a03 e102 d102 5908 9ff6 9901 3107 9ff4 9920
  //   3107 9ff9 9902 3107 9ffa 9903 3107 9ffb b107 9a01 e102 491b 9ff0 b107 9a02 e102 5929 9800 9ff4 3007
  //   6800 9a0c e302 5b31 9964 9a0a 9b02 9c0c 6835 99b4 9a10 9b03 9c18 9800 3100 8801 3200 8801 3300 8801
  //   3400 9908 8801 3100 9ff5 9902 3107 9ff4 9921 3107 9800 b400 9ef1 b106 f104 5949 9920 3107 9ef5 9903
  //   3106 9801 b200 8801 b300 9ef9 3206 9efa 9dfb 9924 3107 9903 3106 b105 9801 e100 495d 992c 3107 9903
  //   3106 b105 9801 e100 4965 8bff 5b59 9920 3107 9ef5 9904 3106 9930 3107 9804 b400 9ef1 b106 a204 f201
  //   5a75 9ef5 9905 3106 9803 b200 9ef9 3206 9934 3107 9efa 9903 3106 9dfb b105 9801 e100 4986 9920 3107
  //   9efa 9902 3106 9ef3 b106 5990 9900 3107 9ef5 990d 3106 9940 3107 7000
endmodule

module MUX2_1 (
  input  B_1,
  input  A_1,
  input  S_1,
  output Y
);

  wire and_1_out, and_2_out, not_1_out;

  not not_1 (not_1_out, S_1);
  and and_1 (and_1_out, B_1, S_1);
  and and_2 (and_2_out, A_1, not_1_out);
  or or_1 (Y, and_1_out, and_2_out);
endmodule

module MUX2_8 (
  input  [7:0] B_8,
  input  [7:0] A_8,
  input  S_1,
  output [7:0] Y_8
);

  MUX2_1 mux2_1_1 (.B_1(B_8[0]), .A_1(A_8[0]), .S_1(S_1), .Y(Y_8[0]));
  MUX2_1 mux2_1_2 (.B_1(B_8[1]), .A_1(A_8[1]), .S_1(S_1), .Y(Y_8[1]));
  MUX2_1 mux2_1_3 (.B_1(B_8[2]), .A_1(A_8[2]), .S_1(S_1), .Y(Y_8[2]));
  MUX2_1 mux2_1_4 (.B_1(B_8[3]), .A_1(A_8[3]), .S_1(S_1), .Y(Y_8[3]));
  MUX2_1 mux2_1_5 (.B_1(B_8[4]), .A_1(A_8[4]), .S_1(S_1), .Y(Y_8[4]));
  MUX2_1 mux2_1_6 (.B_1(B_8[5]), .A_1(A_8[5]), .S_1(S_1), .Y(Y_8[5]));
  MUX2_1 mux2_1_7 (.B_1(B_8[6]), .A_1(A_8[6]), .S_1(S_1), .Y(Y_8[6]));
  MUX2_1 mux2_1_8 (.B_1(B_8[7]), .A_1(A_8[7]), .S_1(S_1), .Y(Y_8[7]));
endmodule

module MUX3_8 (
  input  [7:0] C_8,
  input  [7:0] B_8,
  input  [7:0] A_8,
  input  [1:0] S_2,
  output [7:0] Y_8
);

  wire [7:0] mux2_8_1_y_8;

  MUX2_8 mux2_8_1 (.B_8(B_8), .A_8(A_8), .S_1(S_2[0]), .Y_8(mux2_8_1_y_8));
  MUX2_8 mux2_8_2 (.B_8(C_8), .A_8(mux2_8_1_y_8), .S_1(S_2[1]), .Y_8(Y_8));
endmodule

module MUX8_8 (
  input  [7:0] X7_8,
  input  [7:0] X6_8,
  input  [7:0] X5_8,
  input  [7:0] X4_8,
  input  [7:0] X3_8,
  input  [7:0] X2_8,
  input  [7:0] X1_8,
  input  [7:0] X0_8,
  input  [2:0] S_3,
  output [7:0] Y_8
);

  wire [7:0] mux2_8_1_y_8, mux2_8_2_y_8, mux2_8_3_y_8, mux2_8_4_y_8, mux2_8_5_y_8, mux2_8_6_y_8;

  MUX2_8 mux2_8_1 (.B_8(X7_8), .A_8(X6_8), .S_1(S_3[0]), .Y_8(mux2_8_1_y_8));
  MUX2_8 mux2_8_2 (.B_8(X5_8), .A_8(X4_8), .S_1(S_3[0]), .Y_8(mux2_8_2_y_8));
  MUX2_8 mux2_8_3 (.B_8(X3_8), .A_8(X2_8), .S_1(S_3[0]), .Y_8(mux2_8_3_y_8));
  MUX2_8 mux2_8_4 (.B_8(X1_8), .A_8(X0_8), .S_1(S_3[0]), .Y_8(mux2_8_4_y_8));
  MUX2_8 mux2_8_5 (.B_8(mux2_8_1_y_8), .A_8(mux2_8_2_y_8), .S_1(S_3[1]), .Y_8(mux2_8_5_y_8));
  MUX2_8 mux2_8_6 (.B_8(mux2_8_3_y_8), .A_8(mux2_8_4_y_8), .S_1(S_3[1]), .Y_8(mux2_8_6_y_8));
  MUX2_8 mux2_8_7 (.B_8(mux2_8_5_y_8), .A_8(mux2_8_6_y_8), .S_1(S_3[2]), .Y_8(Y_8));
endmodule

module MUX16_8 (
  input  [7:0] X15_8,
  input  [7:0] X14_8,
  input  [7:0] X13_8,
  input  [7:0] X12_8,
  input  [7:0] X11_8,
  input  [7:0] X10_8,
  input  [7:0] X9_8,
  input  [7:0] X8_8,
  input  [7:0] X7_8,
  input  [7:0] X6_8,
  input  [7:0] X5_8,
  input  [7:0] X4_8,
  input  [7:0] X3_8,
  input  [7:0] X2_8,
  input  [7:0] X1_8,
  input  [7:0] X0_8,
  input  [3:0] S_4,
  output [7:0] Y_8
);

  wire [7:0] mux8_8_1_y_8, mux8_8_2_y_8;

  MUX8_8 mux8_8_1 (
    .X7_8(X15_8), .X6_8(X14_8), .X5_8(X13_8), .X4_8(X12_8), .X3_8(X11_8), .X2_8(X10_8), .X1_8(X9_8),
    .X0_8(X8_8), .S_3(S_4[2:0]), .Y_8(mux8_8_1_y_8));
  MUX8_8 mux8_8_2 (
    .X7_8(X7_8), .X6_8(X6_8), .X5_8(X5_8), .X4_8(X4_8), .X3_8(X3_8), .X2_8(X2_8), .X1_8(X1_8), .X0_8(X0_8),
    .S_3(S_4[2:0]), .Y_8(mux8_8_2_y_8));
  MUX2_8 mux2_8_1 (.B_8(mux8_8_1_y_8), .A_8(mux8_8_2_y_8), .S_1(S_4[3]), .Y_8(Y_8));
endmodule

module DEC3_8 (
  input  E_1,
  input  [2:0] I_3,
  output [7:0] O_8
);

  wire not_1_out, not_2_out, not_3_out, not_4_out, not_6_out, not_7_out, not_8_out, not_9_out, not_10_out,
       not_12_out, not_13_out, not_14_out;

  not not_1 (not_1_out, I_3[0]);
  not not_2 (not_2_out, I_3[1]);
  not not_3 (not_3_out, I_3[1]);
  not not_4 (not_4_out, I_3[0]);
  // NOT_Gate not_5 is placed but not wired
  not not_6 (not_6_out, I_3[2]);
  not not_7 (not_7_out, I_3[2]);
  not not_8 (not_8_out, I_3[0]);
  not not_9 (not_9_out, I_3[2]);
  not not_10 (not_10_out, I_3[1]);
  // NOT_Gate not_11 is placed but not wired
  not not_12 (not_12_out, I_3[2]);
  not not_13 (not_13_out, I_3[1]);
  not not_14 (not_14_out, I_3[0]);
  and and_1 (O_8[7], E_1, I_3[2], I_3[1], I_3[0]);
  and and_2 (O_8[6], E_1, I_3[2], I_3[1], not_1_out);
  and and_3 (O_8[5], E_1, I_3[2], not_2_out, I_3[0]);
  and and_4 (O_8[4], E_1, I_3[2], not_3_out, not_4_out);
  and and_5 (O_8[3], E_1, not_6_out, I_3[1], I_3[0]);
  and and_6 (O_8[2], E_1, not_7_out, I_3[1], not_8_out);
  and and_7 (O_8[1], E_1, not_9_out, not_10_out, I_3[0]);
  and and_8 (O_8[0], E_1, not_12_out, not_13_out, not_14_out);
endmodule

module DEC4_16 (
  input  E_1,
  input  [3:0] I_4,
  output [15:0] O_16
);

  wire and_1_out, and_2_out, not_1_out;

  not not_1 (not_1_out, I_4[3]);
  and and_1 (and_1_out, E_1, not_1_out);
  and and_2 (and_2_out, E_1, I_4[3]);
  DEC3_8 dec3_8_1 (.E_1(and_2_out), .I_3(I_4[2:0]), .O_8(O_16[15:8]));
  DEC3_8 dec3_8_2 (.E_1(and_1_out), .I_3(I_4[2:0]), .O_8(O_16[7:0]));
endmodule

module EQ_3 (
  input  [2:0] B_3,
  input  [2:0] A_3,
  output out_3
);

  wire [2:0] xnor_1_out;

  assign xnor_1_out = ~(B_3 ^ A_3);  // XNOR_Gate xnor_1, 3 bits wide
  and and_1 (out_3, xnor_1_out[0], xnor_1_out[1], xnor_1_out[2]);
endmodule

module EQ_8 (
  input  [7:0] B_8,
  input  [7:0] A_8,
  output EQ_1
);

  wire [7:0] xnor_1_out;

  assign xnor_1_out = ~(B_8 ^ A_8);  // XNOR_Gate xnor_1, 8 bits wide
  and and_1 (EQ_1, xnor_1_out[0], xnor_1_out[1], xnor_1_out[2], xnor_1_out[3], xnor_1_out[4], xnor_1_out[5], xnor_1_out[6], xnor_1_out[7]);
endmodule

module ZERO_8 (
  input  [7:0] A_8,
  output Y_1
);

  nor nor_1 (Y_1, A_8[0], A_8[1], A_8[2], A_8[3], A_8[4], A_8[5], A_8[6], A_8[7]);
endmodule

module REG_FILE (
  input  [2:0] Write_3,
  input  [7:0] Data_8,
  input  [2:0] ReadA_3,
  input  [2:0] ReadB_3,
  input  RegWrite_1,
  input  CLK,
  output [7:0] OP1_8,
  output [7:0] OP2_8
);

  wire and_1_out, and_2_out, and_3_out, and_4_out, and_5_out, and_6_out, and_7_out, and_8_out;
  wire [7:0] dec3_8_1_o_8, R0_q, R1_q, R2_q, R3_q, R4_q, R5_q, R6_q, R7_q;

  DEC3_8 dec3_8_1 (.E_1(1'b1), .I_3(Write_3), .O_8(dec3_8_1_o_8));
  and and_1 (and_1_out, dec3_8_1_o_8[7], RegWrite_1);
  and and_2 (and_2_out, dec3_8_1_o_8[6], RegWrite_1);
  and and_3 (and_3_out, dec3_8_1_o_8[5], RegWrite_1);
  and and_4 (and_4_out, dec3_8_1_o_8[4], RegWrite_1);
  and and_5 (and_5_out, dec3_8_1_o_8[3], RegWrite_1);
  and and_6 (and_6_out, dec3_8_1_o_8[2], RegWrite_1);
  and and_7 (and_7_out, dec3_8_1_o_8[1], RegWrite_1);
  and and_8 (and_8_out, dec3_8_1_o_8[0], RegWrite_1);
  Register R7 (.D(Data_8), .en(and_1_out), .clk(CLK), .Q(R7_q));  // open: clr
  Register R6 (.D(Data_8), .en(and_2_out), .clk(CLK), .Q(R6_q));  // open: clr
  Register R5 (.D(Data_8), .en(and_3_out), .clk(CLK), .Q(R5_q));  // open: clr
  Register R4 (.D(Data_8), .en(and_4_out), .clk(CLK), .Q(R4_q));  // open: clr
  Register R3 (.D(Data_8), .en(and_5_out), .clk(CLK), .Q(R3_q));  // open: clr
  Register R2 (.D(Data_8), .en(and_6_out), .clk(CLK), .Q(R2_q));  // open: clr
  Register R1 (.D(Data_8), .en(and_7_out), .clk(CLK), .Q(R1_q));  // open: clr
  Register R0 (.D(Data_8), .en(and_8_out), .clk(CLK), .Q(R0_q));  // open: clr
  MUX8_8 mux8_8_1 (
    .X7_8(R7_q), .X6_8(R6_q), .X5_8(R5_q), .X4_8(R4_q), .X3_8(R3_q), .X2_8(R2_q), .X1_8(R1_q), .X0_8(R0_q),
    .S_3(ReadA_3), .Y_8(OP1_8));
  MUX8_8 mux8_8_2 (
    .X7_8(R7_q), .X6_8(R6_q), .X5_8(R5_q), .X4_8(R4_q), .X3_8(R3_q), .X2_8(R2_q), .X1_8(R1_q), .X0_8(R0_q),
    .S_3(ReadB_3), .Y_8(OP2_8));
endmodule

module HA_1 (
  input  A_1,
  input  B_1,
  output Sum_1,
  output Cout_1
);

  xor xor_1 (Sum_1, A_1, B_1);
  and and_1 (Cout_1, A_1, B_1);
endmodule

module FA_1 (
  input  Cin_1,
  input  A_1,
  input  B_1,
  output Cout_1,
  output Sum_1
);

  wire ha_1_1_cout_1, ha_1_1_sum_1, ha_1_2_cout_1;

  HA_1 ha_1_1 (.A_1(A_1), .B_1(B_1), .Sum_1(ha_1_1_sum_1), .Cout_1(ha_1_1_cout_1));
  HA_1 ha_1_2 (.A_1(ha_1_1_sum_1), .B_1(Cin_1), .Sum_1(Sum_1), .Cout_1(ha_1_2_cout_1));
  or or_1 (Cout_1, ha_1_2_cout_1, ha_1_1_cout_1);
endmodule

module ADD_8 (
  input  Cin_1,
  input  [7:0] A_8,
  input  [7:0] B_8,
  output Cout_1,
  output [7:0] Sum_8
);

  wire FA0_cout_1, fa_1_1_cout_1, fa_1_2_cout_1, fa_1_3_cout_1, fa_1_4_cout_1, fa_1_5_cout_1, fa_1_6_cout_1;

  FA_1 FA0 (.Cin_1(Cin_1), .A_1(A_8[0]), .B_1(B_8[0]), .Cout_1(FA0_cout_1), .Sum_1(Sum_8[0]));
  FA_1 fa_1_1 (.Cin_1(FA0_cout_1), .A_1(A_8[1]), .B_1(B_8[1]), .Cout_1(fa_1_1_cout_1), .Sum_1(Sum_8[1]));
  FA_1 fa_1_2 (.Cin_1(fa_1_1_cout_1), .A_1(A_8[2]), .B_1(B_8[2]), .Cout_1(fa_1_2_cout_1), .Sum_1(Sum_8[2]));
  FA_1 fa_1_3 (.Cin_1(fa_1_2_cout_1), .A_1(A_8[3]), .B_1(B_8[3]), .Cout_1(fa_1_3_cout_1), .Sum_1(Sum_8[3]));
  FA_1 fa_1_4 (.Cin_1(fa_1_3_cout_1), .A_1(A_8[4]), .B_1(B_8[4]), .Cout_1(fa_1_4_cout_1), .Sum_1(Sum_8[4]));
  FA_1 fa_1_5 (.Cin_1(fa_1_4_cout_1), .A_1(A_8[5]), .B_1(B_8[5]), .Cout_1(fa_1_5_cout_1), .Sum_1(Sum_8[5]));
  FA_1 fa_1_6 (.Cin_1(fa_1_5_cout_1), .A_1(A_8[6]), .B_1(B_8[6]), .Cout_1(fa_1_6_cout_1), .Sum_1(Sum_8[6]));
  FA_1 fa_1_7 (.Cin_1(fa_1_6_cout_1), .A_1(A_8[7]), .B_1(B_8[7]), .Cout_1(Cout_1), .Sum_1(Sum_8[7]));
endmodule

module ALU (
  input  [4:0] aluSignals,
  input  [7:0] A_8,
  input  [7:0] B_8,
  output [7:0] aluResult
);

  wire add_8_1_cout_1;
  wire [0:0] not_1_out;
  wire [2:0] or_2_out;
  wire [7:0] add_8_1_sum_8, and_1_out, B1_out;
  wire [7:7] subtract_out;

  or subtract (subtract_out[7], aluSignals[4], aluSignals[2]);
  assign B1_out = {8{subtract_out[7]}} ^ B_8;  // XOR_Gate B1, 8 bits wide
  assign and_1_out = A_8 & B_8;  // AND_Gate and_1, 8 bits wide
  ADD_8 add_8_1 (.Cin_1(subtract_out[7]), .A_8(A_8), .B_8(B1_out), .Cout_1(add_8_1_cout_1), .Sum_8(add_8_1_sum_8));
  or or_1 (or_2_out[1], aluSignals[1], aluSignals[2]);
  not not_1 (not_1_out[0], add_8_1_cout_1);
  or or_2 (or_2_out[0], aluSignals[0], subtract_out[7]);
  or or_3 (or_2_out[2], aluSignals[3], aluSignals[4]);
  MUX8_8 mux8_8_1 (
    .X7_8({8{1'b0}}), .X6_8({8{1'b0}}), .X5_8({{7{1'b0}}, not_1_out[0]}), .X4_8(and_1_out),
    .X3_8(add_8_1_sum_8), .X2_8(add_8_1_sum_8), .X1_8(B_8), .X0_8({8{1'b0}}), .S_3(or_2_out), .Y_8(aluResult));

  // Notes on the sheet:
  //   isSLTU
  //   isSub
  //   isAdd
  //   isAnd
  //   isPass
  //   isAddorSub
endmodule

module INSTR_DECODE (
  input  [15:0] INSTR_16,
  output [3:0] OPCODE_4,
  output I_1,
  output [2:0] RA_3,
  output [2:0] RB_3,
  output [7:0] IMM_8
);


  assign I_1 = INSTR_16[11];
  assign IMM_8 = INSTR_16[7:0];
  assign OPCODE_4 = INSTR_16[15:12];
  assign RA_3 = INSTR_16[10:8];
  assign RB_3 = INSTR_16[2:0];
endmodule

module CONTROL_UNIT (
  input  [3:0] OPCODE_4,
  input  IMM_1,
  output isBNEZ,
  output isBEQZ,
  output [4:0] aluSignals,
  output isHALT,
  output isLD,
  output isST,
  output isRW,
  output isImm,
  output useA,
  output useB
);

  wire and_1_out, and_2_out, and_8_out, and_15_out, and_16_out, and_17_out, not_1_out, not_2_out, not_3_out,
       not_4_out, not_5_out, not_6_out, not_7_out, not_8_out, or_1_out, or_2_out, or_3_out, xor_1_out;

  not not_1 (not_1_out, OPCODE_4[2]);
  not not_2 (not_2_out, OPCODE_4[3]);
  and and_1 (and_1_out, OPCODE_4[2], not_2_out);
  and and_2 (and_2_out, OPCODE_4[0], OPCODE_4[1], not_1_out);
  xor xor_1 (xor_1_out, OPCODE_4[1], OPCODE_4[0]);
  not not_3 (not_3_out, OPCODE_4[0]);
  and and_3 (isBNEZ, xor_1_out, and_1_out);
  and and_4 (isBEQZ, not_3_out, and_1_out);
  and and_5 (isHALT, OPCODE_4[0], OPCODE_4[1], and_1_out);
  and and_6 (isST, and_2_out, not_2_out);
  and and_7 (isLD, and_2_out, OPCODE_4[3]);
  or or_1 (or_1_out, OPCODE_4[1], OPCODE_4[0]);
  not not_4 (not_4_out, OPCODE_4[1]);
  not not_5 (not_5_out, OPCODE_4[0]);
  and and_8 (and_8_out, OPCODE_4[1], OPCODE_4[0]);
  or or_2 (or_2_out, and_2_out, OPCODE_4[3]);
  not not_6 (not_6_out, IMM_1);
  not not_7 (not_7_out, not_1_out);
  and and_9 (aluSignals[0], or_1_out, not_1_out);
  and and_10 (aluSignals[1], not_4_out, not_5_out);
  and and_11 (aluSignals[2], not_7_out, not_4_out, OPCODE_4[0]);
  and and_12 (aluSignals[3], not_7_out, OPCODE_4[1], not_5_out);
  and and_13 (aluSignals[4], not_7_out, and_8_out);
  and and_14 (useB, or_2_out, not_6_out);
  or or_3 (or_3_out, not_4_out, OPCODE_4[3]);
  not not_8 (not_8_out, OPCODE_4[3]);
  and and_15 (and_15_out, not_7_out, or_3_out);
  and and_16 (and_16_out, aluSignals[1], OPCODE_4[3]);
  and and_17 (and_17_out, not_8_out, and_8_out, not_1_out);
  or or_4 (useA, and_15_out, and_16_out, and_17_out);

  assign isImm = IMM_1;
  assign isRW = OPCODE_4[3];

  // Notes on the sheet:
  //   is_ctrl
  //   is_mem
  //   isPass
  //   isSub
  //   isAdd
  //   isAnd
  //   isSLTU
endmodule

module INC_8 (
  input  [7:0] A_8,
  output Cout_1,
  output [7:0] Sum_8
);

  ADD_8 add_8_1 (.Cin_1(1'b1), .A_8(A_8), .B_8({8{1'b0}}), .Cout_1(Cout_1), .Sum_8(Sum_8));
endmodule

module NEXT_PC (
  input  isBranchTaken,
  input  [7:0] TARGET,
  input  [7:0] PC_8,
  output [7:0] PC_NEXT_8
);

  wire [7:0] inc_8_1_sum_8;

  INC_8 inc_8_1 (.A_8(PC_8), .Sum_8(inc_8_1_sum_8));  // open: Cout_1
  MUX2_8 mux2_8_1 (.B_8(TARGET), .A_8(inc_8_1_sum_8), .S_1(isBranchTaken), .Y_8(PC_NEXT_8));
endmodule

module BRANCH_UNIT (
  input  BNEZ,
  input  BEQZ,
  input  [7:0] A_8,
  output isBranchTaken
);

  wire and_1_out, and_2_out, not_1_out, zero_8_1_y_1;

  ZERO_8 zero_8_1 (.A_8(A_8), .Y_1(zero_8_1_y_1));
  not not_1 (not_1_out, zero_8_1_y_1);
  and and_1 (and_1_out, BNEZ, not_1_out);
  and and_2 (and_2_out, BEQZ, zero_8_1_y_1);
  or or_1 (isBranchTaken, and_1_out, and_2_out);
endmodule

module PERIPHERAL (
  input  [7:0] TEMP_8,
  input  START_1,
  input  DOOR_CLOSED_1,
  input  [1:0] MODE_2,
  input  [7:0] WATER_LEVEL_8,
  input  [7:0] DRUM_RPM_8,
  input  [7:0] P_WDATA_8,
  input  P_WE_1,
  input  [3:0] P_ADDR_4,
  input  CLK,
  input  RESET_1,
  output MOTOR_EN_REQ_1,
  output PUMP_OUT_1,
  output VALVE_IN_1,
  output MOTOR_EN_ACTUAL_1,
  output MOTOR_DIR_1,
  output DOOR_LOCK_1,
  output HEATER_1,
  output BUZZER_1,
  output D_TRIP_1,
  output [7:0] DISPLAY_8,
  output D_PEND_1,
  output D_TIMER_EN_1,
  output D_TIMER_MATCH_1,
  output [7:0] D_TIMER_COUNT_8,
  output [7:0] P_RDATA_8
);

  wire and_2_out, and_3_out, and_4_out, and_5_out, and_6_out, and_7_out, and_8_out, and_9_out, and_10_out,
       eq_8_1_eq_1, not_2_out, not_3_out, not_4_out, not_5_out, not_6_out, not_7_out, not_8_out, or_1_out,
       or_2_out, or_3_out, or_4_out, START_PREV_q, zero_8_1_y_1;
  wire [7:0] and_1_out, inc_8_1_sum_8, LIMIT_q;
  wire [7:7] ACT_q, not_1_out;
  wire [15:0] dec4_16_1_o_16;

  INC_8 inc_8_1 (.A_8(D_TIMER_COUNT_8), .Sum_8(inc_8_1_sum_8));  // open: Cout_1
  not not_1 (not_1_out[7], and_3_out);
  DEC4_16 dec4_16_1 (.E_1(P_WE_1), .I_4(P_ADDR_4), .O_16(dec4_16_1_o_16));
  assign and_1_out = inc_8_1_sum_8 & {8{not_1_out[7]}};  // AND_Gate and_1, 8 bits wide
  or or_1 (or_1_out, D_TIMER_EN_1, and_3_out);
  Register ACT (
    .D({1'b0, P_WDATA_8[6:0]}), .en(dec4_16_1_o_16[4]), .clk(CLK),
    .Q({ACT_q[7], BUZZER_1, DOOR_LOCK_1, PUMP_OUT_1, MOTOR_DIR_1, MOTOR_EN_REQ_1, HEATER_1, VALVE_IN_1}),
    .clr(RESET_1));
  Register DISPLAY (.D(P_WDATA_8), .en(dec4_16_1_o_16[5]), .clk(CLK), .Q(DISPLAY_8), .clr(RESET_1));
  and and_2 (and_2_out, dec4_16_1_o_16[6], P_WDATA_8[0]);
  and and_3 (and_3_out, dec4_16_1_o_16[10], P_WDATA_8[1]);
  Register #(.width(1)) T_EN (.D(P_WDATA_8[0]), .en(dec4_16_1_o_16[10]), .clk(CLK), .Q(D_TIMER_EN_1), .clr(RESET_1));
  Register LIMIT (.D(P_WDATA_8), .en(dec4_16_1_o_16[9]), .clk(CLK), .Q(LIMIT_q), .clr(RESET_1));
  Register COUNTER (.D(and_1_out), .en(or_1_out), .clk(CLK), .Q(D_TIMER_COUNT_8), .clr(RESET_1));
  ZERO_8 zero_8_1 (.A_8(LIMIT_q), .Y_1(zero_8_1_y_1));
  EQ_8 eq_8_1 (.B_8(LIMIT_q), .A_8(inc_8_1_sum_8), .EQ_1(eq_8_1_eq_1));
  not not_2 (not_2_out, zero_8_1_y_1);
  and and_4 (and_4_out, D_TIMER_EN_1, not_2_out, eq_8_1_eq_1);
  or or_2 (or_2_out, D_TIMER_MATCH_1, and_4_out);
  not not_3 (not_3_out, MOTOR_EN_REQ_1);
  Register #(.width(1)) START_PREV (.D(START_1), .en(1'b1), .clk(CLK), .Q(START_PREV_q), .clr(RESET_1));
  Register #(.width(1)) MATCH (.D(and_5_out), .en(1'b1), .clk(CLK), .Q(D_TIMER_MATCH_1), .clr(RESET_1));
  and and_5 (and_5_out, or_2_out, not_1_out[7]);
  not not_4 (not_4_out, DOOR_CLOSED_1);
  not not_5 (not_5_out, START_PREV_q);
  not not_6 (not_6_out, and_2_out);
  and and_6 (and_6_out, not_4_out, MOTOR_EN_REQ_1);
  and and_7 (and_7_out, not_3_out, DOOR_CLOSED_1, and_2_out, D_PEND_1);
  not not_7 (not_7_out, and_7_out);
  and and_8 (and_8_out, START_1, not_5_out);
  or or_3 (or_3_out, D_TRIP_1, and_6_out);
  and and_9 (and_9_out, not_6_out, D_PEND_1);
  and and_10 (and_10_out, or_3_out, not_7_out);
  Register #(.width(1)) TRIP (.D(and_10_out), .en(1'b1), .clk(CLK), .Q(D_TRIP_1), .clr(RESET_1));
  Register #(.width(1)) PEND (.D(or_4_out), .en(1'b1), .clk(CLK), .Q(D_PEND_1), .clr(RESET_1));
  or or_4 (or_4_out, and_8_out, and_9_out);
  not not_8 (not_8_out, D_TRIP_1);
  and and_11 (MOTOR_EN_ACTUAL_1, MOTOR_EN_REQ_1, DOOR_CLOSED_1, not_8_out);
  MUX16_8 mux16_8_1 (
    .X15_8({8{1'b0}}), .X14_8({8{1'b0}}), .X13_8({8{1'b0}}), .X12_8({8{1'b0}}),
    .X11_8({{6{1'b0}}, D_TIMER_EN_1, D_TIMER_MATCH_1}), .X10_8({{7{1'b0}}, D_TIMER_EN_1}), .X9_8(LIMIT_q),
    .X8_8(D_TIMER_COUNT_8), .X7_8({8{1'b0}}), .X6_8({8{1'b0}}), .X5_8(DISPLAY_8),
    .X4_8({ACT_q[7], BUZZER_1, DOOR_LOCK_1, PUMP_OUT_1, MOTOR_DIR_1, MOTOR_EN_REQ_1, HEATER_1, VALVE_IN_1}),
    .X3_8(DRUM_RPM_8), .X2_8(TEMP_8), .X1_8(WATER_LEVEL_8),
    .X0_8({2'b00, D_TRIP_1, D_PEND_1, MODE_2, DOOR_CLOSED_1, START_1}), .S_4(P_ADDR_4), .Y_8(P_RDATA_8));

  // Notes on the sheet:
  //   CLR_1
  //   ACK_1
  //   Z_1
  //   EQ_1
  //   IN_STATUS_8
  //   PADDR_4
endmodule

module MEM_STAGE (
  input  [7:0] ADDR_8,
  input  isLD,
  input  isST,
  input  [7:0] WDATA_8,
  input  [7:0] P_RDATA_8,
  input  CLK,
  output [7:0] RDATA_8,
  output [3:0] P_ADDR_4,
  output P_WE_1,
  output [7:0] P_WDATA_8
);

  wire and_1_out, and_2_out, not_1_out;
  wire [7:0] mux2_8_1_y_8, ram_1_dout;

  and and_1 (and_1_out, ADDR_8[7], ADDR_8[6], ADDR_8[5], ADDR_8[4]);
  not not_1 (not_1_out, ADDR_8[7]);
  and and_2 (and_2_out, isST, not_1_out);
  and and_3 (P_WE_1, and_1_out, isST);
  RAM #(.addrWidth(7), .asyncread("true")) ram_1 (
    .addr(ADDR_8[6:0]), .we(and_2_out), .oe(isLD), .clk(CLK), .din(WDATA_8), .dout(ram_1_dout));
  MUX2_8 mux2_8_1 (.B_8(ram_1_dout), .A_8({8{1'b0}}), .S_1(not_1_out), .Y_8(mux2_8_1_y_8));
  MUX2_8 mux2_8_2 (.B_8(P_RDATA_8), .A_8(mux2_8_1_y_8), .S_1(and_1_out), .Y_8(RDATA_8));

  assign P_ADDR_4 = ADDR_8[3:0];
  assign P_WDATA_8 = WDATA_8;
endmodule

module CPU_SC (
  input  START,
  input  DOOR_CLOSED,
  input  [1:0] MODE,
  input  [7:0] WATER_LEVEL,
  input  [7:0] TEMP,
  input  [7:0] DRUM_RPM,
  input  CLK,
  input  RESET,
  output VALVE_IN,
  output HEATER,
  output MOTOR_EN_REQ,
  output MOTOR_DIR,
  output PUMP_OUT,
  output DOOR_LOCK,
  output BUZZER,
  output MOTOR_EN_ACTUAL,
  output [7:0] DISPLAY,
  output TRIP,
  output START_PEND,
  output [7:0] TIMER_COUNT,
  output TIMER_MATCH,
  output [7:0] PC,
  output [15:0] INSTR,
  output TIMER_EN,
  output HALTED,
  output [7:0] WB_DATA
);

  wire branch_unit_1_isbranchtaken, control_unit_1_isbeqz, control_unit_1_isbnez, control_unit_1_ishalt,
       control_unit_1_isimm, control_unit_1_isld, control_unit_1_isrw, control_unit_1_isst,
       instr_decode_1_i_1, mem_stage_1_p_we_1, not_1_out, not_2_out;
  wire [2:0] instr_decode_1_ra_3, instr_decode_1_rb_3;
  wire [3:0] instr_decode_1_opcode_4, mem_stage_1_p_addr_4;
  wire [4:0] control_unit_1_alusignals;
  wire [7:0] alu_1_aluresult, instr_decode_1_imm_8, mem_stage_1_p_wdata_8, mem_stage_1_rdata_8, mux2_8_1_y_8,
       next_pc_1_pc_next_8, peripheral_1_p_rdata_8, reg_file_1_op1_8, reg_file_1_op2_8;

  NEXT_PC next_pc_1 (
    .isBranchTaken(branch_unit_1_isbranchtaken), .TARGET(instr_decode_1_imm_8), .PC_8(PC),
    .PC_NEXT_8(next_pc_1_pc_next_8));
  Register PC_REG (.D(next_pc_1_pc_next_8), .en(not_1_out), .clk(CLK), .Q(PC), .clr(RESET));
  not not_1 (not_1_out, control_unit_1_ishalt);
  ROM #(.dataWidth(16)) rom_1 (.addr(PC), .data(INSTR));
  Register #(.width(1)) register_1 (.D(1'b1), .en(control_unit_1_ishalt), .clk(CLK), .Q(HALTED), .clr(RESET));
  INSTR_DECODE instr_decode_1 (
    .INSTR_16(INSTR), .OPCODE_4(instr_decode_1_opcode_4), .I_1(instr_decode_1_i_1),
    .RA_3(instr_decode_1_ra_3), .RB_3(instr_decode_1_rb_3), .IMM_8(instr_decode_1_imm_8));
  REG_FILE reg_file_1 (
    .Write_3(instr_decode_1_ra_3), .Data_8(WB_DATA), .ReadA_3(instr_decode_1_ra_3),
    .ReadB_3(instr_decode_1_rb_3), .RegWrite_1(control_unit_1_isrw), .CLK(CLK), .OP1_8(reg_file_1_op1_8),
    .OP2_8(reg_file_1_op2_8));
  CONTROL_UNIT control_unit_1 (
    .OPCODE_4(instr_decode_1_opcode_4), .IMM_1(instr_decode_1_i_1), .isBNEZ(control_unit_1_isbnez),
    .isBEQZ(control_unit_1_isbeqz), .aluSignals(control_unit_1_alusignals), .isHALT(control_unit_1_ishalt),
    .isLD(control_unit_1_isld), .isST(control_unit_1_isst), .isRW(control_unit_1_isrw),
    .isImm(control_unit_1_isimm));  // open: useA, useB
  not not_2 (not_2_out, control_unit_1_isimm);
  BRANCH_UNIT branch_unit_1 (
    .BNEZ(control_unit_1_isbnez), .BEQZ(control_unit_1_isbeqz), .A_8(reg_file_1_op1_8),
    .isBranchTaken(branch_unit_1_isbranchtaken));
  MUX2_8 mux2_8_1 (.B_8(reg_file_1_op2_8), .A_8(instr_decode_1_imm_8), .S_1(not_2_out), .Y_8(mux2_8_1_y_8));
  ALU alu_1 (
    .A_8(reg_file_1_op1_8), .B_8(mux2_8_1_y_8), .aluSignals(control_unit_1_alusignals),
    .aluResult(alu_1_aluresult));
  MEM_STAGE mem_stage_1 (
    .ADDR_8(alu_1_aluresult), .isLD(control_unit_1_isld), .isST(control_unit_1_isst),
    .WDATA_8(reg_file_1_op1_8), .P_RDATA_8(peripheral_1_p_rdata_8), .CLK(CLK), .RDATA_8(mem_stage_1_rdata_8),
    .P_ADDR_4(mem_stage_1_p_addr_4), .P_WE_1(mem_stage_1_p_we_1), .P_WDATA_8(mem_stage_1_p_wdata_8));
  PERIPHERAL peripheral_1 (
    .TEMP_8(TEMP), .START_1(START), .DOOR_CLOSED_1(DOOR_CLOSED), .MODE_2(MODE), .WATER_LEVEL_8(WATER_LEVEL),
    .DRUM_RPM_8(DRUM_RPM), .P_WDATA_8(mem_stage_1_p_wdata_8), .P_WE_1(mem_stage_1_p_we_1),
    .P_ADDR_4(mem_stage_1_p_addr_4), .CLK(CLK), .RESET_1(RESET), .MOTOR_EN_REQ_1(MOTOR_EN_REQ),
    .PUMP_OUT_1(PUMP_OUT), .VALVE_IN_1(VALVE_IN), .MOTOR_EN_ACTUAL_1(MOTOR_EN_ACTUAL),
    .MOTOR_DIR_1(MOTOR_DIR), .DOOR_LOCK_1(DOOR_LOCK), .HEATER_1(HEATER), .BUZZER_1(BUZZER), .D_TRIP_1(TRIP),
    .DISPLAY_8(DISPLAY), .D_PEND_1(START_PEND), .D_TIMER_EN_1(TIMER_EN), .D_TIMER_MATCH_1(TIMER_MATCH),
    .D_TIMER_COUNT_8(TIMER_COUNT), .P_RDATA_8(peripheral_1_p_rdata_8));
  MUX2_8 mux2_8_2 (.B_8(mem_stage_1_rdata_8), .A_8(alu_1_aluresult), .S_1(control_unit_1_isld), .Y_8(WB_DATA));

  // Notes on the sheet:
  //   contents of rom_1 (hex, n*v repeats v):
  //   9800 9ff4 3007 9ffa 3007 9ff5 9901 3107 9ff0 b307 a103 9a03 e102 d102 5908 9ff6 9901 3107 9ff4 9920
  //   3107 9ff9 9902 3107 9ffa 9903 3107 9ffb b107 9a01 e102 491b 9ff0 b107 9a02 e102 5929 9800 9ff4 3007
  //   6800 9a0c e302 5b31 9964 9a0a 9b02 9c0c 6835 99b4 9a10 9b03 9c18 9800 3100 8801 3200 8801 3300 8801
  //   3400 9908 8801 3100 9ff5 9902 3107 9ff4 9921 3107 9800 b400 9ef1 b106 f104 5949 9920 3107 9ef5 9903
  //   3106 9801 b200 8801 b300 9ef9 3206 9efa 9dfb 9924 3107 9903 3106 b105 9801 e100 495d 992c 3107 9903
  //   3106 b105 9801 e100 4965 8bff 5b59 9920 3107 9ef5 9904 3106 9930 3107 9804 b400 9ef1 b106 a204 f201
  //   5a75 9ef5 9905 3106 9803 b200 9ef9 3206 9934 3107 9efa 9903 3106 9dfb b105 9801 e100 4986 9920 3107
  //   9efa 9902 3106 9ef3 b106 5990 9900 3107 9ef5 990d 3106 9940 3107 7000
endmodule

module ID_STAGE (
  input  [15:0] INSTR_16,
  input  [2:0] WB_RD,
  input  [7:0] WB_DATA,
  input  WB_WE,
  input  BYP_EN,
  input  CLK,
  output isBNEZ,
  output isBEQZ,
  output [4:0] aluSignals,
  output isHALT,
  output isLD,
  output isST,
  output isRW,
  output isImm,
  output useA,
  output useB,
  output [2:0] RD,
  output [2:0] RB,
  output [7:0] A,
  output [7:0] B,
  output [7:0] IMM
);

  wire and_1_out, and_2_out, eq_3_1_out_3, eq_3_2_out_3, instr_decode_1_i_1;
  wire [3:0] instr_decode_1_opcode_4;
  wire [7:0] reg_file_1_op1_8, reg_file_1_op2_8;

  INSTR_DECODE instr_decode_1 (
    .INSTR_16(INSTR_16), .OPCODE_4(instr_decode_1_opcode_4), .I_1(instr_decode_1_i_1), .RA_3(RD), .RB_3(RB),
    .IMM_8(IMM));
  REG_FILE reg_file_1 (
    .Write_3(WB_RD), .Data_8(WB_DATA), .ReadA_3(RD), .ReadB_3(RB), .RegWrite_1(WB_WE), .CLK(CLK),
    .OP1_8(reg_file_1_op1_8), .OP2_8(reg_file_1_op2_8));
  CONTROL_UNIT control_unit_1 (
    .OPCODE_4(instr_decode_1_opcode_4), .IMM_1(instr_decode_1_i_1), .isBNEZ(isBNEZ), .isBEQZ(isBEQZ),
    .aluSignals(aluSignals), .isHALT(isHALT), .isLD(isLD), .isST(isST), .isRW(isRW), .isImm(isImm),
    .useA(useA), .useB(useB));
  EQ_3 eq_3_1 (.B_3(RD), .A_3(WB_RD), .out_3(eq_3_1_out_3));
  EQ_3 eq_3_2 (.B_3(RB), .A_3(WB_RD), .out_3(eq_3_2_out_3));
  and and_1 (and_1_out, eq_3_1_out_3, WB_WE, BYP_EN);
  and and_2 (and_2_out, eq_3_2_out_3, WB_WE, BYP_EN);
  MUX2_8 mux2_8_1 (.B_8(WB_DATA), .A_8(reg_file_1_op1_8), .S_1(and_1_out), .Y_8(A));
  MUX2_8 mux2_8_2 (.B_8(WB_DATA), .A_8(reg_file_1_op2_8), .S_1(and_2_out), .Y_8(B));
endmodule

module EX_STAGE (
  input  isBNEZ,
  input  isBEQZ,
  input  [7:0] A,
  input  [7:0] B,
  input  [7:0] IMM,
  input  isImm,
  input  [4:0] aluSignals,
  input  [7:0] FWD_W,
  input  [7:0] FWD_M,
  input  [1:0] SEL_A,
  input  [1:0] SEL_B,
  output isBranchTaken,
  output [7:0] aluResult,
  output [7:0] SD
);

  wire and_1_out, and_2_out, not_1_out, zero_8_1_y_1;
  wire [7:0] mux2_8_1_y_8, mux3_8_2_y_8;

  MUX3_8 mux3_8_1 (.C_8(FWD_W), .B_8(FWD_M), .A_8(A), .S_2(SEL_A), .Y_8(SD));
  MUX3_8 mux3_8_2 (.C_8(FWD_W), .B_8(FWD_M), .A_8(B), .S_2(SEL_B), .Y_8(mux3_8_2_y_8));
  ZERO_8 zero_8_1 (.A_8(SD), .Y_1(zero_8_1_y_1));
  MUX2_8 mux2_8_1 (.B_8(IMM), .A_8(mux3_8_2_y_8), .S_1(isImm), .Y_8(mux2_8_1_y_8));
  not not_1 (not_1_out, zero_8_1_y_1);
  and and_1 (and_1_out, isBNEZ, not_1_out);
  and and_2 (and_2_out, isBEQZ, zero_8_1_y_1);
  ALU alu_1 (.A_8(SD), .B_8(mux2_8_1_y_8), .aluSignals(aluSignals), .aluResult(aluResult));
  or or_1 (isBranchTaken, and_1_out, and_2_out);
endmodule

module IFID_REG (
  input  V_IN,
  input  [15:0] INSTR,
  input  [7:0] PC,
  input  EN,
  input  CLK,
  input  RESET,
  output IFID_V,
  output [15:0] IFID_INSTR,
  output [7:0] IFID_PC
);

  Register #(.width(1)) register_1 (.D(V_IN), .en(EN), .clk(CLK), .Q(IFID_V), .clr(RESET));
  Register #(.width(16)) register_2 (.D(INSTR), .en(EN), .clk(CLK), .Q(IFID_INSTR), .clr(RESET));
  Register register_3 (.D(PC), .en(EN), .clk(CLK), .Q(IFID_PC), .clr(RESET));
endmodule

module IDEX_REG (
  input  V_IN,
  input  [7:0] PC,
  input  isRW,
  input  isImm,
  input  isLD,
  input  isST,
  input  isBEQZ,
  input  isBNEZ,
  input  isHALT,
  input  USE_A,
  input  USE_B,
  input  [4:0] aluSignals,
  input  [2:0] RD,
  input  [2:0] RB,
  input  [7:0] A,
  input  [7:0] B,
  input  [7:0] IMM,
  input  CLK,
  input  RESET,
  output IDEX_V,
  output [7:0] IDEX_PC,
  output IDEX_isRW,
  output IDEX_isImm,
  output IDEX_isLD,
  output IDEX_isST,
  output IDEX_isBEQZ,
  output IDEX_isBNEZ,
  output IDEX_isHALT,
  output IDEX_USE_A,
  output IDEX_USE_B,
  output [4:0] IDEX_aluSignals,
  output [2:0] IDEX_RD,
  output [2:0] IDEX_RB,
  output [7:0] IDEX_A,
  output [7:0] IDEX_B,
  output [7:0] IDEX_IMM
);

  Register #(.width(1)) register_1 (.D(V_IN), .en(1'b1), .clk(CLK), .Q(IDEX_V), .clr(RESET));
  Register register_2 (.D(PC), .en(1'b1), .clk(CLK), .Q(IDEX_PC), .clr(RESET));
  Register #(.width(1)) register_3 (.D(isRW), .en(1'b1), .clk(CLK), .Q(IDEX_isRW), .clr(RESET));
  Register #(.width(1)) register_4 (.D(isImm), .en(1'b1), .clk(CLK), .Q(IDEX_isImm), .clr(RESET));
  Register #(.width(1)) register_5 (.D(isLD), .en(1'b1), .clk(CLK), .Q(IDEX_isLD), .clr(RESET));
  Register #(.width(1)) register_6 (.D(isST), .en(1'b1), .clk(CLK), .Q(IDEX_isST), .clr(RESET));
  Register #(.width(1)) register_7 (.D(isBEQZ), .en(1'b1), .clk(CLK), .Q(IDEX_isBEQZ), .clr(RESET));
  Register #(.width(1)) register_8 (.D(isBNEZ), .en(1'b1), .clk(CLK), .Q(IDEX_isBNEZ), .clr(RESET));
  Register #(.width(1)) register_9 (.D(isHALT), .en(1'b1), .clk(CLK), .Q(IDEX_isHALT), .clr(RESET));
  Register #(.width(1)) register_10 (.D(USE_A), .en(1'b1), .clk(CLK), .Q(IDEX_USE_A), .clr(RESET));
  Register #(.width(1)) register_11 (.D(USE_B), .en(1'b1), .clk(CLK), .Q(IDEX_USE_B), .clr(RESET));
  Register #(.width(5)) register_12 (.D(aluSignals), .en(1'b1), .clk(CLK), .Q(IDEX_aluSignals), .clr(RESET));
  Register #(.width(3)) register_13 (.D(RD), .en(1'b1), .clk(CLK), .Q(IDEX_RD), .clr(RESET));
  Register #(.width(3)) register_14 (.D(RB), .en(1'b1), .clk(CLK), .Q(IDEX_RB), .clr(RESET));
  Register register_15 (.D(A), .en(1'b1), .clk(CLK), .Q(IDEX_A), .clr(RESET));
  Register register_16 (.D(B), .en(1'b1), .clk(CLK), .Q(IDEX_B), .clr(RESET));
  Register register_17 (.D(IMM), .en(1'b1), .clk(CLK), .Q(IDEX_IMM), .clr(RESET));
endmodule

module EXMEM_REG (
  input  V_IN,
  input  [7:0] PC,
  input  isRW,
  input  isLD,
  input  isST,
  input  [2:0] RD,
  input  [7:0] ALU,
  input  [7:0] SD,
  input  CLK,
  input  RESET,
  output EXMEM_V,
  output [7:0] EXMEM_PC,
  output EXMEM_isRW,
  output EXMEM_isLD,
  output EXMEM_isST,
  output [2:0] EXMEM_RD,
  output [7:0] EXMEM_ALU,
  output [7:0] EXMEM_SD
);

  Register #(.width(1)) register_1 (.D(V_IN), .en(1'b1), .clk(CLK), .Q(EXMEM_V), .clr(RESET));
  Register register_2 (.D(PC), .en(1'b1), .clk(CLK), .Q(EXMEM_PC), .clr(RESET));
  Register #(.width(1)) register_3 (.D(isRW), .en(1'b1), .clk(CLK), .Q(EXMEM_isRW), .clr(RESET));
  Register #(.width(1)) register_4 (.D(isLD), .en(1'b1), .clk(CLK), .Q(EXMEM_isLD), .clr(RESET));
  Register #(.width(1)) register_5 (.D(isST), .en(1'b1), .clk(CLK), .Q(EXMEM_isST), .clr(RESET));
  Register #(.width(3)) register_6 (.D(RD), .en(1'b1), .clk(CLK), .Q(EXMEM_RD), .clr(RESET));
  Register register_7 (.D(ALU), .en(1'b1), .clk(CLK), .Q(EXMEM_ALU), .clr(RESET));
  Register register_8 (.D(SD), .en(1'b1), .clk(CLK), .Q(EXMEM_SD), .clr(RESET));
endmodule

module MEMWB_REG (
  input  V_IN,
  input  [7:0] PC,
  input  isRW,
  input  [2:0] RD,
  input  [7:0] DATA,
  input  CLK,
  input  RESET,
  output MEMWB_V,
  output [7:0] MEMWB_PC,
  output MEMWB_isRW,
  output [2:0] MEMWB_RD,
  output [7:0] MEMWB_DATA
);

  Register #(.width(1)) register_1 (.D(V_IN), .en(1'b1), .clk(CLK), .Q(MEMWB_V), .clr(RESET));
  Register register_2 (.D(PC), .en(1'b1), .clk(CLK), .Q(MEMWB_PC), .clr(RESET));
  Register #(.width(1)) register_3 (.D(isRW), .en(1'b1), .clk(CLK), .Q(MEMWB_isRW), .clr(RESET));
  Register #(.width(3)) register_4 (.D(RD), .en(1'b1), .clk(CLK), .Q(MEMWB_RD), .clr(RESET));
  Register register_5 (.D(DATA), .en(1'b1), .clk(CLK), .Q(MEMWB_DATA), .clr(RESET));
endmodule

module FORWARD (
  input  IDEX_USE_A,
  input  IDEX_V,
  input  EXMEM_isLD,
  input  IDEX_USE_B,
  input  [2:0] EXMEM_RD,
  input  [2:0] IDEX_RD,
  input  EXMEM_V,
  input  EXMEM_isRW,
  input  [2:0] MEMWB_RD,
  input  MEMWB_V,
  input  MEMWB_isRW,
  input  [2:0] IDEX_RB,
  output LOADFWD,
  output [1:0] SEL_A,
  output [1:0] SEL_B
);

  wire and_2_out, and_4_out, and_5_out, and_6_out, eq_3_1_out_3, eq_3_2_out_3, eq_3_3_out_3, eq_3_4_out_3,
       not_1_out, not_2_out, or_1_out;

  EQ_3 eq_3_1 (.B_3(EXMEM_RD), .A_3(IDEX_RD), .out_3(eq_3_1_out_3));
  EQ_3 eq_3_2 (.B_3(MEMWB_RD), .A_3(IDEX_RD), .out_3(eq_3_2_out_3));
  EQ_3 eq_3_3 (.B_3(EXMEM_RD), .A_3(IDEX_RB), .out_3(eq_3_3_out_3));
  EQ_3 eq_3_4 (.B_3(MEMWB_RD), .A_3(IDEX_RB), .out_3(eq_3_4_out_3));
  and and_1 (SEL_A[0], eq_3_1_out_3, EXMEM_V, EXMEM_isRW);
  and and_2 (and_2_out, eq_3_2_out_3, MEMWB_V, MEMWB_isRW);
  and and_3 (SEL_B[0], eq_3_3_out_3, EXMEM_V, EXMEM_isRW);
  and and_4 (and_4_out, eq_3_4_out_3, MEMWB_V, MEMWB_isRW);
  and and_5 (and_5_out, SEL_A[0], IDEX_USE_A);
  and and_6 (and_6_out, SEL_B[0], IDEX_USE_B);
  not not_1 (not_1_out, SEL_A[0]);
  not not_2 (not_2_out, SEL_B[0]);
  or or_1 (or_1_out, and_5_out, and_6_out);
  and and_7 (SEL_A[1], not_1_out, and_2_out);
  and and_8 (SEL_B[1], not_2_out, and_4_out);
  and and_9 (LOADFWD, or_1_out, IDEX_V, EXMEM_isLD);
endmodule

module HAZARD (
  input  IFID_V,
  input  IDEX_isLD,
  input  [2:0] RA,
  input  [2:0] IDEX_RD,
  input  USE_A,
  input  USE_B,
  input  [2:0] RB,
  input  IDEX_V,
  input  TAKEN,
  input  IDEX_isHALT,
  input  HALTED,
  output STALL,
  output IFID_EN,
  output IDEX_VIN,
  output REDIRECT,
  output FLUSH,
  output HALT_NOW,
  output PC_EN,
  output IFID_VIN
);

  wire and_1_out, and_2_out, and_5_out, eq_3_1_out_3, eq_3_2_out_3, not_1_out, not_3_out, not_4_out,
       or_1_out, or_3_out, or_4_out;

  EQ_3 eq_3_1 (.B_3(RA), .A_3(IDEX_RD), .out_3(eq_3_1_out_3));
  EQ_3 eq_3_2 (.B_3(RB), .A_3(IDEX_RD), .out_3(eq_3_2_out_3));
  and and_1 (and_1_out, eq_3_1_out_3, USE_A);
  and and_2 (and_2_out, USE_B, eq_3_2_out_3);
  and and_3 (REDIRECT, IDEX_V, TAKEN);
  and and_4 (HALT_NOW, IDEX_V, IDEX_isHALT);
  or or_1 (or_1_out, and_1_out, and_2_out);
  or or_2 (FLUSH, REDIRECT, HALT_NOW);
  and and_5 (and_5_out, IFID_V, IDEX_isLD, IDEX_V);
  not not_1 (not_1_out, FLUSH);
  and and_6 (STALL, and_5_out, or_1_out, not_1_out);
  not not_2 (IFID_EN, STALL);
  or or_3 (or_3_out, STALL, HALT_NOW, HALTED);
  not not_3 (not_3_out, FLUSH);
  not not_4 (not_4_out, or_3_out);
  or or_4 (or_4_out, FLUSH, HALTED);
  and and_7 (IDEX_VIN, IFID_EN, IFID_V, not_3_out);
  not not_5 (IFID_VIN, or_4_out);
  or or_5 (PC_EN, not_4_out, REDIRECT);
endmodule
